# Fritzing sketch Esquema (saved by Fritzing 0.9.3b)
breadboards: 1

parts:
  MEGA_2560 = Arduino Mega 2560 (Rev3)
  R1 = Resistor [tolerance=±5% resistance=10k package=THT]
  DHT1 = DHT11 Humitidy and Temperature Sensor
  DS1 = DS18B20 1-Wire Temperature Sensor [part_number=DS18B20]
  R2 = Resistor [tolerance=±5% resistance=4.7k package=THT]
  BMP180 = Barometric Pressure Sensor - BMP180 Breakout (GY-68)
  Componente1 = LCD1602-I2C
  Water_Sensor = Water Level Sensor
  Buzzer = Piezo Speaker
  R3 = Photocell (LDR) [package=THT]
  R4 = Photocell (LDR) [package=THT]
  R5 = Photocell (LDR) [package=THT]
  R6 = Resistor [tolerance=±5% resistance=10k package=THT]
  R7 = Resistor [tolerance=±5% resistance=10k package=THT]
  R8 = Resistor [tolerance=±5% resistance=10k package=THT]
  S1 = Pololu QTR-8 Reflectabce Sensor array [package=THT]

nets:
  N1: MEGA_2560.A0, S1.pin12
  N2: MEGA_2560.A1, R3.pin_1, R6.Pin_0
  N3: MEGA_2560.A2, R4.pin_1, R8.Pin_0
  N4: MEGA_2560.A3, R5.pin_1, R7.Pin_0
  N5: MEGA_2560.D21/SCL, BMP180.SCL, Componente1.SCL
  N6: MEGA_2560.D20/SDA, MEGA_2560.SDA, BMP180.SDA, Componente1.SDA
  GND: MEGA_2560.GND, DHT1.GND, DS1.GND, BMP180.GND, Componente1.GND, Water_Sensor.GND, Buzzer.pin1, R3.pin_0, S1.pin1, S1.pin15
  VCC: MEGA_2560.5V, R1.Pin_1, DHT1.VDD, DS1.VDD, R2.Pin_1, BMP180.VCC, Componente1.VCC, Water_Sensor.VCC, R6.Pin_1, R7.Pin_1, R8.Pin_1, S1.pin2, S1.pin14
  N7: MEGA_2560.D33, DS1.DQ, R2.Pin_0
  N8: MEGA_2560.D37, R1.Pin_0, DHT1.DATA
  N9: MEGA_2560.D41, Water_Sensor.SIG
  N10: MEGA_2560.D45, Buzzer.pin2
  N11: R4.pin_0, R5.pin_0

custom parts:
  DHT11 Humitidy and Temperature Sensor: DHT11 Humidity and Temperature Sensor
  LCD1602-I2C: A standard character display, usually with 2x16 characters. Comes in many colors with LCM1602 IIC attached.
  Water Level Sensor: A water level sensor. This sensor operates at 3V to 5V. The Sig (signal) pin outputs an analogue signal that is in proportion to the amount of water in contact with the sensor.
